# Fritzing sketch encoders (saved by Fritzing 0.9.3b)

parts:
  due = Arduino Due (Rev2b)
  mot_di = Motorreductor DC con encoder incremental (conector a la izquierda)
  mot_dd = Motorreductor DC con encoder incremental (conector a la izquierda)
  mot_ti = Motorreductor DC con encoder incremental (conector a la izquierda)
  mot_td = Motorreductor DC con encoder incremental (conector a la izquierda)

nets:
  VCC: due.IOREF, mot_di.VCC, mot_dd.VCC, mot_ti.VCC, mot_td.VCC
  GND: due.GND, mot_di.GND, mot_dd.GND, mot_ti.GND, mot_td.GND
  N1: due.D22, mot_di.A
  N2: due.D23, mot_di.B
  N3: due.D24, mot_dd.A
  N4: due.D25, mot_dd.B
  N5: due.D26, mot_ti.A
  N6: due.D27, mot_ti.B
  N7: due.D28, mot_td.A
  N8: due.D29, mot_td.B

custom parts:
  Motorreductor DC con encoder incremental (conector a la izquierda): Motorreductor DC con encoder incremental (conector a la izquierda) (pieza genérica dibujada para el auto 4WD)
