# Fritzing sketch energia (saved by Fritzing 0.9.3b)

parts:
  pack = Portapilas 4× 18650
  sd300 = Step-down DC-DC 300 W (12 V para los motores)
  sdusb = Step-down con salida USB-C (5 V para la Raspberry Pi)
  pi = Raspberry Pi 5  # not connected
  bts_di = BTS7960
  mot_di = Motorreductor DC con encoder incremental
  bts_ti = BTS7960
  mot_ti = Motorreductor DC con encoder incremental
  bts_dd = BTS7960
  mot_dd = Motorreductor DC con encoder incremental
  bts_td = BTS7960
  mot_td = Motorreductor DC con encoder incremental

nets:
  N1: pack.+, sd300.IN+, sdusb.IN+
  N2: pack.-, sd300.IN-, sdusb.IN-
  N3: sd300.OUT+, bts_di.pin11, bts_ti.pin11, bts_dd.pin11, bts_td.pin11
  N4: sd300.OUT-, bts_di.pin12, bts_ti.pin12, bts_dd.pin12, bts_td.pin12
  N5: bts_di.pin9, mot_di.M+
  N6: bts_di.pin10, mot_di.M-
  N7: bts_ti.pin9, mot_ti.M+
  N8: bts_ti.pin10, mot_ti.M-
  N9: bts_dd.pin9, mot_dd.M+
  N10: bts_dd.pin10, mot_dd.M-
  N11: bts_td.pin9, mot_td.M+
  N12: bts_td.pin10, mot_td.M-

custom parts:
  Portapilas 4× 18650: Portapilas 4× 18650 (pieza genérica dibujada para el auto 4WD)
  Step-down DC-DC 300 W (12 V para los motores): Step-down DC-DC 300 W (12 V para los motores) (pieza genérica dibujada para el auto 4WD)
  Step-down con salida USB-C (5 V para la Raspberry Pi): Step-down con salida USB-C (5 V para la Raspberry Pi) (pieza genérica dibujada para el auto 4WD)
  Raspberry Pi 5: The RPi5, a faster version of the awesome Raspberry Pi4B ARM Board with 40 pin gpio.
  BTS7960: BTS7960 43A Peak Power H-Bridge PWM Motor Driver
  Motorreductor DC con encoder incremental: Motorreductor DC con encoder incremental (pieza genérica dibujada para el auto 4WD)
