# Fritzing sketch motores (saved by Fritzing 0.9.3b)

parts:
  due = Arduino Due (Rev2b)
  bts_di = BTS7960
  bts_dd = BTS7960
  bts_ti = BTS7960
  bts_td = BTS7960

nets:
  N1: due.D8_PWM, bts_ti.pin2
  N2: due.D9_PWM, bts_dd.pin2
  N3: due.D10_PWM/SS0, bts_dd.pin1
  N4: due.D11_PWM, bts_di.pin1
  N5: due.D12_PWM, bts_di.pin2
  N6: due.GND, bts_di.pin8, bts_dd.pin8, bts_ti.pin8, bts_td.pin8
  N7: due.D5_PWM, bts_td.pin2
  N8: due.D6_PWM, bts_td.pin1
  N9: due.D7_PWM, bts_ti.pin1
  N10: due.5V, bts_di.pin3, bts_di.pin4, bts_di.pin7, bts_dd.pin3, bts_dd.pin4, bts_dd.pin7, bts_ti.pin3, bts_ti.pin4, bts_ti.pin7, bts_td.pin3, bts_td.pin4, bts_td.pin7

custom parts:
  BTS7960: BTS7960 43A Peak Power H-Bridge PWM Motor Driver
