# Fritzing sketch sensores (saved by Fritzing 0.9.3b)

parts:
  due = Arduino Due (Rev2b)
  imu = SparkFun IMU Breakout - MPU-9250
  pi = Raspberry Pi 5  # not connected
  lidar = RPlidar A1M8 [package=THT]  # not connected

nets:
  N1: due.D20/SDA3, imu.SDA/SDI
  N2: due.D21/SCL3, imu.SCL/SCLK
  N3: due.IOREF, imu.VDD
  GND: due.GND, imu.GND

custom parts:
  Raspberry Pi 5: The RPi5, a faster version of the awesome Raspberry Pi4B ARM Board with 40 pin gpio.
  RPlidar A1M8: .The RPLIDAR A1 is the next generation low cost 360 degree 2D laser scanner (LIDAR) solution developed by SLAMTEC. It can take up to 4000 samples of laser ranging per second with high rotation speed. And equipped with SLAMTEC patented OPTMAG technology, it breakouts the life limitation of traditional LIDAR system so as to work stably for a long time.
